# Fritzing sketch Server_wiring (saved by Fritzing 0.9.3b)
breadboards: 2

parts:
  Componente1 = Adafruit Feather HUZZAH ESP8266 [part_number="Adafruit #2821"]
  U1 = Vibration Motor- ROB-08449 [package=vibe-motor-10mm]
  U2 = Vibration Motor- ROB-08449 [package=vibe-motor-10mm]
  U3 = Vibration Motor- ROB-08449 [package=vibe-motor-10mm]
  U4 = Vibration Motor- ROB-08449 [package=vibe-motor-10mm]
  U5 = Vibration Motor- ROB-08449 [package=vibe-motor-10mm]
  U6 = Vibration Motor- ROB-08449 [package=vibe-motor-10mm]
  Mod1 = Raspberry Pi Pico
  Componente2 = Motor Driver 1A Dual TB6612FNG  # not connected

nets:
  N1: Componente1.GPIO12/MISO, U2.-
  N2: Componente1.GPIO13/MOSI, U3.-
  N3: Componente1.GPIO14/SCK, U1.-
  N4: Componente1.GND, U1.+, U2.+, U3.+, U4.+, U5.+, U6.+
  N5: Componente1.GPIO2, U5.-
  N6: Componente1.GPIO5/SCL, U4.-
  N7: Componente1.GPIO4/SDA, U6.-
  N8: Mod1.pin_3, Mod1.pin_8, Mod1.pin_13, Mod1.pin_18, Mod1.pin_23, Mod1.pin_28, Mod1.pin_33, Mod1.pin_38

custom parts:
  Adafruit Feather HUZZAH ESP8266: his is the Adafruit Feather HUZZAH ESP8266 - our take on an 'all-in-one' ESP8266 WiFi development board with built in USB and battery charging. Its an ESP8266 WiFi module with all the extras you need, ready to rock! We have other boards in the Feather family, check'em out here. At the Feather HUZZAH's heart is an ESP8266 WiFi microcontroller clocked at 80 MHz and at 3.3V logic. This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
  Raspberry Pi Pico: Raspberry Pi Pico. Based around the RP2040 microcontroller the Pico is a low cost microcontroller device bringing Raspberry Pi quality, cost, and easy of use to the microcontroller space. Jan 2021, Split part in to two versions: tht (this one) and SMD. This one will drill holes for a .1 in header in pcb to allow plugging in the module as well as providing pads to solder the module to the top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
