# Fritzing sketch Server_wiring (saved by Fritzing 0.9.3b)
breadboards: 2

parts:
  Componente1 = Adafruit Feather HUZZAH ESP8266 [part_number="Adafruit #2821"]
  U1 = Vibration Motor- ROB-08449 [package=vibe-motor-10mm]
  U2 = Vibration Motor- ROB-08449 [package=vibe-motor-10mm]
  U3 = Vibration Motor- ROB-08449 [package=vibe-motor-10mm]
  U4 = Vibration Motor- ROB-08449 [package=vibe-motor-10mm]
  U5 = Vibration Motor- ROB-08449 [package=vibe-motor-10mm]
  U6 = Vibration Motor- ROB-08449 [package=vibe-motor-10mm]
  Mod1 = Raspberry Pi Pico
  Componente2 = Motor Driver 1A Dual TB6612FNG  # not connected
  M1 = DC Motor  # not connected
  BATT1 = 4xAA Switchable Battery Pack w/Bare Wire
  M2 = RioRand LM2596
  M3 = RioRand LM2596
  Q1 = TRANSISTOR_NPN [package=to-92-ammo]
  R1 = Resistor [tolerance=±5% resistance=100 package=THT]
  R2 = Resistor [tolerance=±5% resistance=100k package=THT]
  U7 = RELAY [package=relay-g5q]
  R3 = Heating Pad
  U8 = SWITCH-SPST-2 [package=switch-spst-vertical]
  M4 = RioRand LM2596
  BATT2 = 4xAA Switchable Battery Pack w/Bare Wire
  Componente3 = Bluetooth HC-05 Macho

nets:
  N1: Componente1.TXD, Mod1.pin_7
  N2: Componente1.RXD, Mod1.pin_6
  N3: Componente1.GPIO12/MISO, U2.-
  N4: Componente1.GPIO13/MOSI, U3.-
  N5: Componente1.GPIO14/SCK, U1.-
  N6: Componente1.GPIO15, U5.-
  N7: Componente1.GPIO5/SCL, U4.-
  N8: Componente1.GPIO4/SDA, U6.-
  N9: U1.+, U2.+, U3.+, U4.+, U5.+, U6.+, M2.Pin_4, Q1.E, BATT2.NEG
  N10: Mod1.pin_1, Componente3.RXD
  N11: Mod1.pin_2, Componente3.TXD
  N12: Mod1.pin_3, Mod1.pin_8, Mod1.pin_13, Mod1.pin_18, Mod1.pin_23, Mod1.pin_28, Mod1.pin_33, Mod1.pin_38, Mod1.pin_42, M3.Pin_4, R3.pin_1, M4.Pin_4
  N13: Mod1.pin_4, R1.Pin_1
  N14: Mod1.pin_39, R2.Pin_1, U7.COIL2, M4.Pin_3, Componente3.VCC
  N15: BATT1.POS, U8.O
  N16: BATT1.NEG, M2.Pin_2, M3.Pin_2, M4.Pin_2
  N17: M2.Pin_1, M3.Pin_1, U8.P, M4.Pin_1
  N18: M3.Pin_3, Componente3.GND
  N19: Q1.B, R1.Pin_0
  N20: Q1.C, R2.Pin_0, U7.COIL1
  N21: U7.MAIN, BATT2.POS
  N22: U7.NO, R3.pin_0

notes:
  3.7V
  6.0V
  5.0V
  1.50cm
  1.90cm
  Power Bank

custom parts:
  Adafruit Feather HUZZAH ESP8266: his is the Adafruit Feather HUZZAH ESP8266 - our take on an 'all-in-one' ESP8266 WiFi development board with built in USB and battery charging. Its an ESP8266 WiFi module with all the extras you need, ready to rock! We have other boards in the Feather family, check'em out here. At the Feather HUZZAH's heart is an ESP8266 WiFi microcontroller clocked at 80 MHz and at 3.3V logic. This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
  Raspberry Pi Pico: Raspberry Pi Pico. Based around the RP2040 microcontroller the Pico is a low cost microcontroller device bringing Raspberry Pi quality, cost, and easy of use to the microcontroller space. Jan 2021, Split part in to two versions: tht (this one) and SMD. This one will drill holes for a .1 in header in pcb to allow plugging in the module as well as providing pads to solder the module to the top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
  4xAA Switchable Battery Pack w/Bare Wire: 4xAA Switchable Battery Pack with Bare Wire connection
  Heating Pad: A thermoresistant material with an embeded conductor that dissipates electrical energy into heat.
